# Fritzing sketch ZHAW_SimpleSafe (saved by Fritzing 1.0.6)
breadboards: 1

parts:
  RFID1 = RFID RC522 Module [package=THT]
  Part1 = Arduino Mega 2560 (Rev3)
  C1 = Electrolytic Capacitor [capacitance=0.1mF voltage=50V package="100 mil [THT, electrolytic]"]
  YwRobot_Power_Supply1 = YwRobot Breadboard Power Supply [part_number=545043]
  Keypad4x1 = Membran Keypad 4x4
  Part2 = InvenSense MPU6050
  LED1 = LED - 5mm [color="Red (633nm)" current=0.030A package="5 mm [THT]"]
  LED2 = LED - 5mm [color="Yellow (585nm)" current=30mA package="5 mm [THT]"]
  LED3 = LED - 5mm [color="Green (555nm)" current=0.030A package="5 mm [THT]"]
  R1 = Resistor [tolerance=±5% power=0.25W resistance=1k package=THT]
  R2 = Resistor [tolerance=±5% power=0.25W resistance=1k package=THT]
  R3 = Resistor [tolerance=±5% power=0.25W resistance=1k package=THT]
  Part3 = KY-006 Passive Buzzer Module [package="Breakout board"]
  S2 = Pushbutton [package="[THT]"]
  R4 = Resistor [tolerance=±5% resistance=10k power=0W package="2010 [SMD]"]
  C2 = Electrolytic Capacitor [capacitance=100nF voltage=50V package="100 mil [THT, electrolytic]"]
  R5 = Rotary Potentiometer (Small) [maximum_resistance=10kΩ knob_status=50% power=0.5W package=THT]
  M3 = Dagu DGServo 9g (Top view) [part_number=RS001B]
  R6 = Photocell (LDR) [power=0.25W dark_resistance_@0.01lx=300kΩ light_resistance_@100lx=400Ω luminance=10lx package=THT]
  R7 = Resistor [tolerance=±5% power=0.25W resistance=47k package=THT]
  Q1 = NPN-Transistor [package="SOT-23 [SMD]"]
  R8 = Resistor [tolerance=±5% power=0.25W resistance=1k package=THT]
  LCD2004-I2C1 = LCD2004-I2C

nets:
  N1: RFID1.NSS, Part1.D9_PWM
  N2: RFID1.SCK, Part1.D52
  N3: RFID1.MOSI, Part1.D51
  N4: RFID1.MISO, Part1.D50
  GND: RFID1.GND, C1.-, YwRobot_Power_Supply1.GND#11, YwRobot_Power_Supply1.GND#12, LED1.cathode, LED2.cathode, LED3.cathode, R4.Pin_1, C2.-, M3.gnd, R6.pin_1, Q1.2, LCD2004-I2C1.GND
  N5: RFID1.RST, Part1.D8_PWM
  VCC: RFID1.VCC, C1.+, YwRobot_Power_Supply1.VCC#5, YwRobot_Power_Supply1.VCC#6, Part3.S, S2.Pin_1, S2.Pin_2, R5.wiper, M3.vcc, R7.Pin_0, LCD2004-I2C1.VCC
  N6: Part1.A14, R6.pin_0, R7.Pin_1
  N7: Part1.A15, R5.leg2
  N8: Part1.D21/SCL, Part1.SCL, Part2.SCL, LCD2004-I2C1.SCL
  N9: Part1.D20/SDA, Part1.SDA, Part2.SDA, LCD2004-I2C1.SDA
  N10: Part1.D10_PWM, M3.pulse
  N11: Part1.D2_PWM, R3.Pin_1
  N12: Part1.D3_PWM, R2.Pin_1
  N13: Part1.D4_PWM, R1.Pin_1
  N14: Part1.D7_PWM, R8.Pin_0
  N15: Part1.D22, Keypad4x1.Pin1
  N16: Part1.D23, Keypad4x1.Pin2
  N17: Part1.D24, Keypad4x1.Pin3
  N18: Part1.D25, Keypad4x1.Pin4
  N19: Part1.D26, Keypad4x1.Pin5
  N20: Part1.D27, Keypad4x1.Pin6
  N21: Part1.D28, Keypad4x1.Pin7
  N22: Part1.D29, Keypad4x1.Pin8
  N23: Part1.D36, S2.Pin_3, S2.Pin_4, R4.Pin_0, C2.+
  N24: YwRobot_Power_Supply1.VCC#9, YwRobot_Power_Supply1.VCC#10, Part2.VCC
  N25: YwRobot_Power_Supply1.GND#13, YwRobot_Power_Supply1.GND#14, Part2.GND
  N26: LED1.anode, R1.Pin_0
  N27: LED2.anode, R2.Pin_0
  N28: LED3.anode, R3.Pin_0
  N29: Part3.-, Q1.1
  N30: Q1.0, R8.Pin_1

custom parts:
  RFID RC522 Module: The RC522 is a 13.56MHz RFID module that is based on the MFRC522 controller from NXP semiconductors. The module can supports I2C, SPI and UART and normally is shipped with a RFID card and key fob. It is commonly used in attendance systems and other person/object identification applications.
  YwRobot Breadboard Power Supply: The YwRobot Breadboard Power Supply (MB-V2) has two power rails; they can be 5V or 3V3. Power to the module can be provided through the female USB socket or through the A10 (female) 2.1mm power jack.
  Membran Keypad 4x4: Membrane Keypad 4x4 Matrix
  KY-006 Passive Buzzer Module: Passive Piezoelectric Buzzer Module Keyes KY-006, it can produce a range of sound tones depending on the input frequency.
  LCD2004-I2C: A standard character display with 4x20 characters. Comes in many colors with LCM2004 IIC attached.
